# Fritzing sketch ATECC108 (saved by Fritzing 0.8.3b)
breadboards: 1

parts:
  ATECC108 = IC, DIP package, 8 pins [chip_label=IC]
  BeagleBone1 = BeagleBone Black
  R1 = Resistor [tolerance=±5% resistance=4.7k package=THT]
  R2 = Resistor [tolerance=±5% resistance=4.7k package=THT]

nets:
  N1: ATECC108.pin4, BeagleBone1.no_name_yet#1
  N2: ATECC108.pin5, BeagleBone1.no_name_yet#20, R1.Pin_0
  N3: ATECC108.pin6, BeagleBone1.no_name_yet#19, R2.Pin_0
  N4: ATECC108.pin8, BeagleBone1.no_name_yet#3, R1.Pin_1, R2.Pin_1

custom parts:
  BeagleBone Black: BeagleBone Black rev. A5B
